// Logisim project neocore_cpu_8bits.circ as structural Verilog: 1 circuit, main circuit main
module main (
  input  MAR_Load,
  input  RAM_Read_MBR,
  input  IR_Load,
  input  PC_Inc,
  input  AC_Exec,
  output [7:0] Monitor
);

  wire CLOCK_out, undriven;
  wire [7:0] adder_1_out, MAR_q, MBR_q, PC_p3, ram_1_p2;

  Clock CLOCK (.out(CLOCK_out));
  Register MAR (.D(PC_p3), .en(MAR_Load), .Q(MAR_q), .clk(CLOCK_out));  // open: clr
  // Counter PC: pin names not known; wires that end beside it: PC_Inc, CLOCK_out, PC_p3
  Register IR (.D(MBR_q), .en(IR_Load), .clk(undriven));  // open: Q, clr
  Register MBR (.D(ram_1_p2), .en(RAM_Read_MBR), .Q(MBR_q), .clk(CLOCK_out));  // open: clr
  // RAM #(.asynch("true"), .databus("bibus")) ram_1: pin names not known; wires that end beside it: MAR_q, ram_1_p2
  Adder adder_1 (.a(MBR_q), .b(Monitor), .out(adder_1_out));  // open: cin, cout
  Register ACUMULADOR (.D(adder_1_out), .en(AC_Exec), .Q(Monitor), .clk(CLOCK_out));  // open: clr
endmodule
