// Logisim project neocore_cpu.circ as structural Verilog: 1 circuit, main circuit main
module main (
  input  [7:0] Teclado,
  input  MAR_Load,
  input  RAM_Read_MBR,
  input  IR_Load,
  input  PC_Inc,
  input  AC_Exec,
  output [7:0] Monitor
);

  wire [7:0] adder_1_out, IR_q, MAR_q, MBR_q, PC_q, RAMDOM_MEMORY_dout;

  Clock clock_1 (.out(AC_Exec));
  Register MAR (.D(PC_q), .en(AC_Exec), .clk(AC_Exec), .Q(MAR_q));  // open: clr
  Counter PC (.count(AC_Exec), .Q(PC_q), .clk(AC_Exec));  // open: load, D, carry, up, clr
  Register IR (.D(MBR_q), .en(AC_Exec), .clk(AC_Exec), .Q(IR_q));  // open: clr
  Register MBR (.D(RAMDOM_MEMORY_dout), .en(AC_Exec), .clk(AC_Exec), .Q(MBR_q));  // open: clr
  RAM RAMDOM_MEMORY (.addr(MAR_q), .oe(AC_Exec), .din(Teclado), .dout(RAMDOM_MEMORY_dout));  // open: we, clk
  Adder adder_1 (.a(MBR_q), .b(Monitor), .out(adder_1_out));  // open: cin, cout
  Register AC (.D(adder_1_out), .en(AC_Exec), .clk(AC_Exec), .Q(Monitor));  // open: clr

  assign IR_Load = AC_Exec;
  assign MAR_Load = AC_Exec;
  assign PC_Inc = AC_Exec;
  assign RAM_Read_MBR = AC_Exec;

  // Notes on the sheet:
  //   CLOCK
  //   Cache L1
  //   Decoder
  //   UC
  //   RAM
  //   ULA
endmodule
